# Fritzing sketch ManPram (saved by Fritzing 0.8.7b)
circuit board: 8.46667cm x 5.64444cm
breadboards: 1

parts:
  Part1 = Arduino Uno (Rev3)
  R1 = Resistor [tolerance=±5% resistance=220 package=THT]
  R2 = Resistor [tolerance=±5% resistance=220 package=THT]
  R3 = Resistor [tolerance=±5% resistance=220 package=THT]
  LED1 = RGB LED (com. anode, rbg) [package="5 mm [THT]"]
  T1 = LM35 Temperature Sensor [package="TO92 [THT]"]
  U1 = POT [package=pot_mammoth]

nets:
  N1: Part1.A0, U1.A
  N2: Part1.A1, T1.Vout
  N3: Part1.D3_PWM, R3.Pin_0
  N4: Part1.D5_PWM, R2.Pin_0
  N5: Part1.D6_PWM, R1.Pin_0
  N6: Part1.3V3, T1.+Vs
  N7: Part1.5V, U1.S
  GND: Part1.GND, LED1.common_anode, T1.GND, U1.E
  N8: R1.Pin_1, LED1.red_cathode
  N9: R2.Pin_1, LED1.green_cathode
  N10: R3.Pin_1, LED1.blue_cathode
